# Fritzing sketch projeFritzing (saved by Fritzing 0.9.4)
breadboards: 1

parts:
  LCD1 = LCD screen
  Matrix_keypad1 = KEYPAD 4x4
  PIR1 = PIR sensor
  SERVO1 = Tower Pro SG90 servo [part_number=101246]
  VCC1 = 4 x AAA Battery Mount
  U1 = PIC16F874A/877A [package=dil40]
  C1 = Ceramic Capacitor [capacitance=15pF package="100 mil [THT, multilayer]"]
  C2 = Ceramic Capacitor [capacitance=15pF package="100 mil [THT, multilayer]"]
  XTAL1 = Crystal [frequency="4 MHz" package=THT]
  U4 = POT [package=pot_mammoth]
  Parça1 = RFID-RC522-v2

nets:
  GND: LCD1.VSS, LCD1.R/W, PIR1.GND, SERVO1.GND, VCC1.-, C1.0, C2.1, Parça1.GND
  VDD: LCD1.VDD, PIR1.VDD, SERVO1.+5V, VCC1.+, U4.E
  N1: LCD1.V0, U4.S, U4.A
  N2: LCD1.RS, U1.RD4/PSP4
  N3: LCD1.E, U1.RD5/PSP5
  N4: LCD1.DB4, U1.RD0/PSP0
  N5: LCD1.DB5, U1.RD1/PSP1
  N6: LCD1.DB6, U1.RD2/PSP2
  N7: LCD1.DB7, U1.RD3/PSP3
  N8: Matrix_keypad1.row1, U1.RC0/T1OSO/T1CKI
  N9: Matrix_keypad1.row2, U1.RC1/T1OSI/CCP2
  N10: Matrix_keypad1.row3, U1.RC2/CCP1
  N11: Matrix_keypad1.row4, U1.RC3/SCK/SCL
  N12: PIR1.SIG, U1.RE2/CS/AN7
  N13: SERVO1.Signal, U1.RD6/PSP6
  N14: U1.RE0/RD/AN5, Parça1.RST
  N15: U1.RE1/WR/AN6, Parça1.IRQ
  N16: U1.OSC1/CLKI, C1.1, XTAL1.pin_0
  N17: U1.OSC2/CLKO, C2.0, XTAL1.pin_1
  N18: U1.RC4/SDI/SDA, Parça1.MOSI
  N19: U1.RC5/SDO, Parça1.MISO
  N20: U1.RC6/TX/CK, Parça1.SCK
  N21: U1.RD7/PSP7, Parça1.3.3V

custom parts:
  KEYPAD 4x4: Matrix keypad 16 buttons, 4 rows x 4 columns
  Tower Pro SG90 servo: Original file by John De Cristofaro http://www.adafruit.com/products/1449 Adafruit Feedback Servo (Small) Edited by: e-radionica.com 28/9/2015
  PIC16F874A/877A: Microchip 6-bit
  RFID-RC522-v2: A simple China made RFID-RC522 Reader; do check the pin labels, as this is a MFRC522 based clone.
